// Digital circuit CPU.dig as structural Verilog
module CPU (
  input  WE,
  input  WE_2,
  input  WE_3,
  input  OE,
  input  OE_2,
  input  OE_3,
  input  OE_4,
  input  WE_4,
  input  OE_5,
  input  OE_6,
  input  WE_5,
  input  WE_6,
  input  OE_7,
  input  EN,
  input  OE_8,
  input  WE_7,
  input  OE_9,
  input  [7:0] test_data,
  input  OE_10,
  output [7:0] RegA,
  output [7:0] RegA_2,
  output [7:0] ALU_result,
  output carry,
  output [7:0] output_reg,
  output [7:0] IR,
  output [7:0] MBR,
  output ovf,
  output [3:0] PC,
  output [3:0] MAR
);

  wire alu_1_p6, clock, RegA_p5, RegB_p5;
  wire [3:0] \_4位寄存器_1_p5 ;
  wire [7:0] \IR_CPU_指令寄存器_p3 , \IR_CPU_指令寄存器_p5 ;

  Button button_1 (.out(clock));
  // _8位寄存器 IR_CPU_指令寄存器: pin names not known; wires that end beside it: WE_3, clock, \IR_CPU_指令寄存器_p3 , OE_5, \IR_CPU_指令寄存器_p5 , IR
  // _8位寄存器 RegA: pin names not known; wires that end beside it: WE, clock, \IR_CPU_指令寄存器_p3 , OE_2, RegA_p5, RegA
  // _8位寄存器 RegB: pin names not known; wires that end beside it: WE_2, clock, \IR_CPU_指令寄存器_p3 , OE_3, RegB_p5, RegA_2
  Counter #(.Bits(2)) counter_1 (.en(EN), .C(clock), .clr(1'b0), .out(PC[1:0]), .ovf(ovf));
  // ALU alu_1: pin names not known; wires that end beside it: RegA_p5, RegB_p5, OE, ALU_result, carry, alu_1_p6
  assign \IR_CPU_指令寄存器_p5 [3:0] = OE_8 ? {2'b00, PC[1:0]} : 4'bz;  // Driver driver_1
  // _4位寄存器 _4位寄存器_1: pin names not known; wires that end beside it: WE_7, clock, \IR_CPU_指令寄存器_p5 [3:0], OE_9, \_4位寄存器_1_p5 , MAR
  // _8位寄存器 _8位寄存器_1: pin names not known; wires that end beside it: WE_4, clock, alu_1_p6, OE_4, \IR_CPU_指令寄存器_p3 , output_reg
  assign \IR_CPU_指令寄存器_p3  = OE_10 ? test_data : 8'bz;  // Driver driver_2
  EEPROMDualPort #(.AddrBits(4), .Bits(8)) eepromdualport_1 (
    .A(\_4位寄存器_1_p5 ), .Din(\IR_CPU_指令寄存器_p3 ), .str(WE_6), .C(clock), .ld(OE_7), .D(\IR_CPU_指令寄存器_p3 ));
  // _8位寄存器 _8位寄存器_2: pin names not known; wires that end beside it: WE_5, clock, \IR_CPU_指令寄存器_p3 , OE_6, \IR_CPU_指令寄存器_p3 , MBR

  assign PC[3:2] = 2'b00;

  // Notes on the sheet:
  //   PC
  //   CPU内部地址总线
  //   MAR 内存地址寄存器
  //   Output Reg
  //   CPU外部地址总线
  //   内部数据总线
  //   contents of eepromdualport_1 (hex, n*v repeats v):
  //   e,1f,20,3f,10*0,3,8
  //   MBR
  //   外部数据总线
endmodule
