// Digital circuit CPU_Auto.dig as structural Verilog
module CPU_Auto (
  input  clock,
  output [7:0] RegA,
  output [7:0] RegB,
  output [7:0] ALU_result,
  output carry,
  output [7:0] output_reg,
  output [7:0] MBR,
  output ovf,
  output [3:0] PC,
  output [3:0] MAR,
  output [3:0] opcode,
  output out_11,
  output [2:0] out_12
);

  wire _0, _1, _2, _3, _4, _5, _6, _7, _8, _9, _10, _11, _12, _13, _14, _15, _16, alu_1_p6, RegA_p5, RegB_p5;
  wire [3:0] \_4位寄存器_1_p5 , \IR_CPU_指令寄存器_p6 ;
  wire [7:0] \IR_CPU_指令寄存器_p3 , \IR_CPU_指令寄存器_p5 ;

  Counter #(.Bits(3)) counter_1 (.en(1'b1), .C(clock), .clr(1'b0), .out(out_12), .ovf(out_11));
  LookUpTable #(.Bits(17)) lookuptable_1 (
    .in0(out_12[0]), .in1(out_12[1]), .in2(out_12[2]), .in3(opcode[0]), .in4(opcode[1]),
    .out({_16, _15, _14, _13, _12, _11, _10, _9, _8, _7, _6, _5, _4, _3, _2, _1, _0}));
  // _8位寄存器 IR_CPU_指令寄存器: pin names not known; wires that end beside it: _2, clock, \IR_CPU_指令寄存器_p3 , _3, \IR_CPU_指令寄存器_p5 , {opcode, \IR_CPU_指令寄存器_p6 }
  // _8位寄存器 RegA: pin names not known; wires that end beside it: _4, clock, \IR_CPU_指令寄存器_p3 , _5, RegA_p5, RegA
  // _8位寄存器 RegB: pin names not known; wires that end beside it: _6, clock, \IR_CPU_指令寄存器_p3 , _7, RegB_p5, RegB
  Counter #(.Bits(2)) counter_2 (.en(_1), .C(clock), .clr(1'b0), .out(PC[1:0]), .ovf(ovf));
  // ALU alu_1: pin names not known; wires that end beside it: RegA_p5, RegB_p5, _8, ALU_result, carry, alu_1_p6
  assign \IR_CPU_指令寄存器_p5 [3:0] = _0 ? {2'b00, PC[1:0]} : 4'bz;  // Driver driver_1
  // _4位寄存器 _4位寄存器_1: pin names not known; wires that end beside it: _9, clock, \IR_CPU_指令寄存器_p5 [3:0], _10, \_4位寄存器_1_p5 , MAR
  // _8位寄存器 _8位寄存器_1: pin names not known; wires that end beside it: _11, clock, alu_1_p6, _12, \IR_CPU_指令寄存器_p3 , output_reg
  EEPROMDualPort #(.AddrBits(4), .Bits(8)) eepromdualport_1 (
    .A(\_4位寄存器_1_p5 ), .Din(\IR_CPU_指令寄存器_p3 ), .str(_13), .C(clock), .ld(_14), .D(\IR_CPU_指令寄存器_p3 ));
  // _8位寄存器 _8位寄存器_2: pin names not known; wires that end beside it: _15, clock, \IR_CPU_指令寄存器_p3 , _16, \IR_CPU_指令寄存器_p3 , MBR

  assign PC[3:2] = 2'b00;

  // Notes on the sheet:
  //   clock: Hz: 10
  //   contents of lookuptable_1 (hex, n*v repeats v):
  //   201,2,c400,10004,208,c400,10010,0,201,2,c400,10004,208,c400,10040
  //   ,0,201,2,c400,10004,9a0,0,0,0,201,2,c400,10004,9208,12400
  //   OE
  //   EN
  //   WE
  //   PC
  //   CPU内部地址总线
  //   MAR 内存地址寄存器
  //   Output Reg
  //   CPU外部地址总线
  //   内部数据总线
  //   contents of eepromdualport_1 (hex, n*v repeats v):
  //   e,1f,20,3f,10*0,3,11
  //   MBR
  //   外部数据总线
endmodule
