// Digital circuit Eight registers.dig as structural Verilog
module Eight_registers (
  input  WE,
  input  clock,
  input  [7:0] Din,
  input  OE,
  output [7:0] Dout,
  output [7:0] stored_data
);

  Register #(.Bits(8)) register_1 (.D(Din), .C(clock), .en(WE), .Q(stored_data));
  assign Dout = OE ? stored_data : 8'bz;  // Driver driver_1
endmodule
